// Logisim project single_cycle_cpu.circ as structural Verilog: 14 circuits, main circuit Registers
module main (
  output [31:0] out_1,
  output [1:0] out_2,
  output [31:0] out_3,
  output out_4,
  output [31:0] out_5,
  output [31:0] out_6,
  output [23:0] out_7,
  output [31:0] out_8
);

  wire and_1_out, clk, controlunit_1_alusrc, controlunit_1_branch, controlunit_1_memread,
       controlunit_1_memwrite, controlunit_1_regwrite, logic_unit_1_zero;
  wire [1:0] controlunit_1_aluop, controlunit_1_immsel;
  wire [2:0] alucontrol_1_alu_sel;
  wire [3:0] ram_1_dout, ram_1_dout_2, ram_1_dout_3, ram_1_dout_4, ram_1_dout_5, ram_1_dout_6, ram_1_dout_7,
       ram_1_dout_8;
  wire [31:0] multiplexer_2_out, multiplexer_3_out, registers_1_rs1_out, registers_1_rs2_out, shifter_1_out,
       z32b_adder_2_sum;
  wire [31:24] logic_unit_1_d_out;

  Clock clock_1 (.out(clk));
  PC pc_1 (.d_in(out_5), .clk(clk), .d_out(out_3));  // open: clr
  z32B_Adder z32b_adder_1 (.a(out_3), .b(32'h1), .sum(out_1));  // open: c_out, c_in
  InstrMem instrmem_1 (.readAddr(out_3), .instruction(out_6));
  ControlUnit controlunit_1 (
    .Branch(controlunit_1_branch), .ALUOp(controlunit_1_aluop), .MemtoReg(out_2),
    .MemWrite(controlunit_1_memwrite), .MemRead(controlunit_1_memread), .ALUSrc(controlunit_1_alusrc),
    .RegWrite(controlunit_1_regwrite), .instruction(out_6), .Jump(out_4), .ImmSel(controlunit_1_immsel));  // open: out_2
  Shifter #(.width(32)) shifter_1 (.in(out_8), .\dist (5'b00001), .out(shifter_1_out));
  ImmGen immgen_1 (.instruction(out_6), .ImmSel(controlunit_1_immsel), .imm_out(out_8));
  z32B_Adder z32b_adder_2 (.a(out_3), .b(shifter_1_out), .sum(z32b_adder_2_sum));  // open: c_out, c_in
  Registers registers_1 (
    .clk(clk), .read_address(out_6[11:7]), .rs1_address(out_6[19:15]), .rs2_out(registers_1_rs2_out),
    .data_in(multiplexer_3_out), .rs2_address(out_6[24:20]), .write_enable(controlunit_1_regwrite),
    .rs1_out(registers_1_rs1_out));  // open: clr
  Hex_Digit_Display hex_digit_display_1 (.value(ram_1_dout_8));  // open: dp
  Multiplexer #(.width(32), .enable("false")) multiplexer_1 (
    .in0(out_1), .in1(z32b_adder_2_sum), .out(out_5), .sel(and_1_out));
  and and_1 (and_1_out, controlunit_1_branch, logic_unit_1_zero);
  Multiplexer #(.width(32), .enable("false")) multiplexer_2 (
    .in0(registers_1_rs2_out), .in1(out_8), .out(multiplexer_2_out), .sel(controlunit_1_alusrc));
  Hex_Digit_Display hex_digit_display_2 (.value(ram_1_dout_7));  // open: dp
  Hex_Digit_Display hex_digit_display_3 (.value(ram_1_dout_6));  // open: dp
  Hex_Digit_Display hex_digit_display_4 (.value(ram_1_dout_5));  // open: dp
  Hex_Digit_Display hex_digit_display_5 (.value(ram_1_dout_4));  // open: dp
  Hex_Digit_Display hex_digit_display_6 (.value(ram_1_dout_2));  // open: dp
  Hex_Digit_Display hex_digit_display_7 (.value(ram_1_dout));  // open: dp
  ALUControl alucontrol_1 (.instruction(out_6), .ALU_op(controlunit_1_aluop), .ALU_Sel(alucontrol_1_alu_sel));
  Logic_Unit logic_unit_1 (
    .d_out({logic_unit_1_d_out, out_7}), .d_in_b(multiplexer_2_out), .d_in_a(registers_1_rs1_out),
    .ALU_selection(alucontrol_1_alu_sel), .zero(logic_unit_1_zero));  // open: overflow, out_7, out_8, out_9
  Hex_Digit_Display hex_digit_display_8 (.value(ram_1_dout_3));  // open: dp
  RAM #(.addrWidth(24), .dataWidth(32), .databus("bibus")) ram_1 (
    .addr(out_7), .we(controlunit_1_memwrite), .oe(controlunit_1_memread), .clk(clk),
    .din(registers_1_rs2_out),
    .dout({ram_1_dout_8, ram_1_dout_7, ram_1_dout_6, ram_1_dout_5, ram_1_dout_4, ram_1_dout, ram_1_dout_2, ram_1_dout_3}));
  Multiplexer #(.select(2), .width(32), .enable("false")) multiplexer_3 (
    .in0({logic_unit_1_d_out, out_7}),
    .in1({ram_1_dout_8, ram_1_dout_7, ram_1_dout_6, ram_1_dout_5, ram_1_dout_4, ram_1_dout, ram_1_dout_2, ram_1_dout_3}),
    .in2(out_1), .out(multiplexer_3_out), .sel(out_2));  // open: in3
endmodule

module Registers (
  input  [31:0] data_in,
  input  [4:0] rs1_address,
  input  [4:0] rs2_address,
  input  [4:0] read_address,
  input  write_enable,
  input  clk,
  input  clr,
  output [31:0] rs1_out,
  output [31:0] rs2_out
);

  wire decoder_1_out0, decoder_1_out1, decoder_1_out2, decoder_1_out3, decoder_1_out4, decoder_1_out5,
       decoder_1_out6, decoder_1_out7, decoder_1_out8, decoder_1_out9, decoder_1_out10, decoder_1_out11,
       decoder_1_out12, decoder_1_out13, decoder_1_out14, decoder_1_out15, decoder_1_out16, decoder_1_out17,
       decoder_1_out18, decoder_1_out19, decoder_1_out20, decoder_1_out21, decoder_1_out22, decoder_1_out23,
       decoder_1_out24, decoder_1_out25, decoder_1_out26, decoder_1_out27, decoder_1_out28, decoder_1_out29,
       decoder_1_out30, decoder_1_out31;
  wire [31:0] x0_q, x1_q, x2_q, x3_q, x4_q, x5_q, x6_q, x7_q, x8_q, x9_q, x10_q, x11_q, x12_q, x13_q, x14_q,
       x15_q, x16_q, x17_q, x18_q, x19_q, x20_q, x21_q, x22_q, x23_q, x24_q, x25_q, x26_q, x27_q, x28_q,
       x29_q, x30_q, x31_q;

  Decoder #(.select(5)) decoder_1 (
    .out0(decoder_1_out0), .out1(decoder_1_out1), .out2(decoder_1_out2), .out3(decoder_1_out3),
    .out4(decoder_1_out4), .out5(decoder_1_out5), .out6(decoder_1_out6), .out7(decoder_1_out7),
    .out8(decoder_1_out8), .out9(decoder_1_out9), .out10(decoder_1_out10), .out11(decoder_1_out11),
    .out12(decoder_1_out12), .out13(decoder_1_out13), .out14(decoder_1_out14), .out15(decoder_1_out15),
    .out16(decoder_1_out16), .out17(decoder_1_out17), .out18(decoder_1_out18), .out19(decoder_1_out19),
    .out20(decoder_1_out20), .out21(decoder_1_out21), .out22(decoder_1_out22), .out23(decoder_1_out23),
    .out24(decoder_1_out24), .out25(decoder_1_out25), .out26(decoder_1_out26), .out27(decoder_1_out27),
    .out28(decoder_1_out28), .out29(decoder_1_out29), .out30(decoder_1_out30), .out31(decoder_1_out31),
    .sel(read_address), .en(write_enable));
  Register #(.width(32)) x0 (.D({32{1'b0}}), .en(decoder_1_out0), .clk(clk), .Q(x0_q), .clr(clr));
  Register #(.width(32)) x1 (.D(data_in), .en(decoder_1_out1), .clk(clk), .Q(x1_q), .clr(clr));
  Register #(.width(32)) x2 (.D(data_in), .en(decoder_1_out2), .clk(clk), .Q(x2_q), .clr(clr));
  Register #(.width(32)) x3 (.D(data_in), .en(decoder_1_out3), .clk(clk), .Q(x3_q), .clr(clr));
  Register #(.width(32)) x4 (.D(data_in), .en(decoder_1_out4), .clk(clk), .Q(x4_q), .clr(clr));
  Register #(.width(32)) x5 (.D(data_in), .en(decoder_1_out5), .clk(clk), .Q(x5_q), .clr(clr));
  Register #(.width(32)) x6 (.D(data_in), .en(decoder_1_out6), .clk(clk), .Q(x6_q), .clr(clr));
  Register #(.width(32)) x7 (.D(data_in), .en(decoder_1_out7), .clk(clk), .Q(x7_q), .clr(clr));
  Register #(.width(32)) x8 (.D(data_in), .en(decoder_1_out8), .clk(clk), .Q(x8_q), .clr(clr));
  Register #(.width(32)) x9 (.D(data_in), .en(decoder_1_out9), .clk(clk), .Q(x9_q), .clr(clr));
  Register #(.width(32)) x10 (.D(data_in), .en(decoder_1_out10), .clk(clk), .Q(x10_q), .clr(clr));
  Register #(.width(32)) x11 (.D(data_in), .en(decoder_1_out11), .clk(clk), .Q(x11_q), .clr(clr));
  Register #(.width(32)) x12 (.D(data_in), .en(decoder_1_out12), .clk(clk), .Q(x12_q), .clr(clr));
  Register #(.width(32)) x13 (.D(data_in), .en(decoder_1_out13), .clk(clk), .Q(x13_q), .clr(clr));
  Register #(.width(32)) x14 (.D(data_in), .en(decoder_1_out14), .clk(clk), .Q(x14_q), .clr(clr));
  Register #(.width(32)) x15 (.D(data_in), .en(decoder_1_out15), .clk(clk), .Q(x15_q), .clr(clr));
  Register #(.width(32)) x16 (.D(data_in), .en(decoder_1_out16), .clk(clk), .Q(x16_q), .clr(clr));
  Register #(.width(32)) x17 (.D(data_in), .en(decoder_1_out17), .clk(clk), .Q(x17_q), .clr(clr));
  Register #(.width(32)) x18 (.D(data_in), .en(decoder_1_out18), .clk(clk), .Q(x18_q), .clr(clr));
  Register #(.width(32)) x19 (.D(data_in), .en(decoder_1_out19), .clk(clk), .Q(x19_q), .clr(clr));
  Register #(.width(32)) x20 (.D(data_in), .en(decoder_1_out20), .clk(clk), .Q(x20_q), .clr(clr));
  Register #(.width(32)) x21 (.D(data_in), .en(decoder_1_out21), .clk(clk), .Q(x21_q), .clr(clr));
  Register #(.width(32)) x22 (.D(data_in), .en(decoder_1_out22), .clk(clk), .Q(x22_q), .clr(clr));
  Register #(.width(32)) x23 (.D(data_in), .en(decoder_1_out23), .clk(clk), .Q(x23_q), .clr(clr));
  Register #(.width(32)) x24 (.D(data_in), .en(decoder_1_out24), .clk(clk), .Q(x24_q), .clr(clr));
  Register #(.width(32)) x25 (.D(data_in), .en(decoder_1_out25), .clk(clk), .Q(x25_q), .clr(clr));
  Register #(.width(32)) x26 (.D(data_in), .en(decoder_1_out26), .clk(clk), .Q(x26_q), .clr(clr));
  Register #(.width(32)) x27 (.D(data_in), .en(decoder_1_out27), .clk(clk), .Q(x27_q), .clr(clr));
  Register #(.width(32)) x28 (.D(data_in), .en(decoder_1_out28), .clk(clk), .Q(x28_q), .clr(clr));
  Register #(.width(32)) x29 (.D(data_in), .en(decoder_1_out29), .clk(clk), .Q(x29_q), .clr(clr));
  Register #(.width(32)) x30 (.D(data_in), .en(decoder_1_out30), .clk(clk), .Q(x30_q), .clr(clr));
  Register #(.width(32)) x31 (.D(data_in), .en(decoder_1_out31), .clk(clk), .Q(x31_q), .clr(clr));
  Multiplexer #(.select(5), .width(32), .enable("false")) multiplexer_1 (
    .in0(x0_q), .in1(x1_q), .in2(x2_q), .in3(x3_q), .in4(x4_q), .in5(x5_q), .in6(x6_q), .in7(x7_q),
    .in8(x8_q), .in9(x9_q), .in10(x10_q), .in11(x11_q), .in12(x12_q), .in13(x13_q), .in14(x14_q),
    .in15(x15_q), .in16(x16_q), .in17(x17_q), .in18(x18_q), .in19(x19_q), .in20(x20_q), .in21(x21_q),
    .in22(x22_q), .in23(x23_q), .in24(x24_q), .in25(x25_q), .in26(x26_q), .in27(x27_q), .in28(x28_q),
    .in29(x29_q), .in30(x30_q), .in31(x31_q), .out(rs1_out), .sel(rs1_address));
  Multiplexer #(.select(5), .width(32), .enable("false")) multiplexer_2 (
    .in0(x0_q), .in1(x1_q), .in2(x2_q), .in3(x3_q), .in4(x4_q), .in5(x5_q), .in6(x6_q), .in7(x7_q),
    .in8(x8_q), .in9(x9_q), .in10(x10_q), .in11(x11_q), .in12(x12_q), .in13(x13_q), .in14(x14_q),
    .in15(x15_q), .in16(x16_q), .in17(x17_q), .in18(x18_q), .in19(x19_q), .in20(x20_q), .in21(x21_q),
    .in22(x22_q), .in23(x23_q), .in24(x24_q), .in25(x25_q), .in26(x26_q), .in27(x27_q), .in28(x28_q),
    .in29(x29_q), .in30(x30_q), .in31(x31_q), .out(rs2_out), .sel(rs2_address));

  // Other names for the same wires on the sheet: d_in[31:0] = data_in
endmodule

module Logic_Unit (
  input  [2:0] ALU_selection,
  input  [31:0] d_in_a,
  input  [31:0] d_in_b,
  output overflow,
  output [31:0] d_out,
  output zero,
  output [31:0] out_7,
  output [31:0] out_8,
  output [31:0] out_9
);

  wire and_2_out, and_3_out, comparator_1_lt, z32b_adder_1_c_out;
  wire [31:0] bit_extender_1_out, xor_1_out, xor_2_out, z32b_adder_1_sum;

  assign out_7 = d_in_a & d_in_b;  // AND_Gate and_1, 32 bits wide
  assign out_8 = d_in_a | d_in_b;  // OR_Gate or_1, 32 bits wide
  assign xor_1_out = d_in_a ^ d_in_b;  // XOR_Gate xor_1, 32 bits wide
  Comparator #(.width(32)) comparator_1 (.a(d_in_a), .b(d_in_b), .lt(comparator_1_lt));  // open: gt, eq
  assign bit_extender_1_out = {{31{comparator_1_lt}}, comparator_1_lt};  // Bit_Extender bit_extender_1
  assign xor_2_out = d_in_b ^ {32{ALU_selection[0]}};  // XOR_Gate xor_2, 32 bits wide
  z32B_Adder z32b_adder_1 (
    .c_out(z32b_adder_1_c_out), .c_in(ALU_selection[0]), .a(d_in_a), .b(xor_2_out), .sum(z32b_adder_1_sum));
  and and_2 (and_2_out, ~z32b_adder_1_c_out, ALU_selection[0]);  // AND_Gate
  and and_3 (and_3_out, z32b_adder_1_c_out, ~ALU_selection[0]);  // AND_Gate
  or or_2 (overflow, and_2_out, and_3_out);
  Multiplexer #(.select(3), .width(32), .enable("false")) multiplexer_1 (
    .in0(z32b_adder_1_sum), .in1(z32b_adder_1_sum), .in2(out_7), .in3(out_8), .in4(xor_1_out),
    .in5(bit_extender_1_out), .out(d_out), .sel(ALU_selection));  // open: in6, in7
  Comparator #(.width(32)) comparator_2 (.a(d_out), .b({32{1'b0}}), .eq(zero));  // open: gt, lt

  assign out_9 = out_8;

  // Other names for the same wires on the sheet: alu_out[31:0] = d_out

  // Notes on the sheet:
  //   arithmetic
endmodule

module z1B_Adder (
  input  a,
  input  b,
  input  c_in,
  output sum,
  output c_out
);

  wire and_1_out, and_2_out, xor_1_out;

  xor xor_1 (xor_1_out, a, b);
  xor xor_2 (sum, xor_1_out, c_in);
  and and_1 (and_1_out, a, b);
  and and_2 (and_2_out, xor_1_out, c_in);
  or or_1 (c_out, and_1_out, and_2_out);
endmodule

module z2B_Adder (
  input  [1:0] a,
  input  [1:0] b,
  input  c_in,
  output [1:0] sum,
  output c_out
);

  wire z1b_adder_1_c_out;

  z1B_Adder z1b_adder_1 (.a(a[0]), .b(b[0]), .c_in(c_in), .sum(sum[0]), .c_out(z1b_adder_1_c_out));
  z1B_Adder z1b_adder_2 (.a(a[1]), .b(b[1]), .c_in(z1b_adder_1_c_out), .sum(sum[1]), .c_out(c_out));
endmodule

module z4B_Adder (
  input  [3:0] a,
  input  [3:0] b,
  input  c_in,
  output [3:0] sum,
  output c_out
);

  wire z2b_adder_1_c_out;

  z2B_Adder z2b_adder_1 (.a(a[1:0]), .b(b[1:0]), .c_in(c_in), .sum(sum[1:0]), .c_out(z2b_adder_1_c_out));
  z2B_Adder z2b_adder_2 (.a(a[3:2]), .b(b[3:2]), .c_in(z2b_adder_1_c_out), .sum(sum[3:2]), .c_out(c_out));
endmodule

module z8B_Adder (
  input  [7:0] a,
  input  [7:0] b,
  input  c_in,
  output [7:0] sum,
  output c_out
);

  wire z4b_adder_1_c_out;

  z4B_Adder z4b_adder_1 (.a(a[3:0]), .b(b[3:0]), .c_in(c_in), .sum(sum[3:0]), .c_out(z4b_adder_1_c_out));
  z4B_Adder z4b_adder_2 (.a(a[7:4]), .b(b[7:4]), .c_in(z4b_adder_1_c_out), .sum(sum[7:4]), .c_out(c_out));
endmodule

module z16B_Adder (
  input  [15:0] a,
  input  [15:0] b,
  input  c_in,
  output [15:0] sum,
  output c_out
);

  wire z8b_adder_1_c_out;

  z8B_Adder z8b_adder_1 (.a(a[7:0]), .b(b[7:0]), .c_in(c_in), .sum(sum[7:0]), .c_out(z8b_adder_1_c_out));
  z8B_Adder z8b_adder_2 (.a(a[15:8]), .b(b[15:8]), .c_in(z8b_adder_1_c_out), .sum(sum[15:8]), .c_out(c_out));
endmodule

module z32B_Adder (
  input  [31:0] a,
  input  [31:0] b,
  input  c_in,
  output [31:0] sum,
  output c_out
);

  wire z16b_adder_1_c_out;

  z16B_Adder z16b_adder_1 (.a(a[15:0]), .b(b[15:0]), .c_in(c_in), .sum(sum[15:0]), .c_out(z16b_adder_1_c_out));
  z16B_Adder z16b_adder_2 (.a(a[31:16]), .b(b[31:16]), .c_in(z16b_adder_1_c_out), .sum(sum[31:16]), .c_out(c_out));
endmodule

module ImmGen (
  input  [31:0] instruction,
  input  [1:0] ImmSel,
  output [31:0] imm_out
);

  wire [0:0] undriven;
  wire [31:0] bit_extender_1_out, bit_extender_2_out, bit_extender_3_out, bit_extender_4_out;

  assign bit_extender_1_out = {{20{instruction[31]}}, instruction[31:20]};  // Bit_Extender bit_extender_1
  assign bit_extender_2_out = {{20{instruction[31]}}, {instruction[31:25], instruction[11:7]}};  // Bit_Extender bit_extender_2
  assign bit_extender_3_out = {{20{instruction[31]}}, {instruction[31], instruction[7], instruction[30:25], instruction[11:8]}};  // Bit_Extender bit_extender_3
  assign bit_extender_4_out = {{12{instruction[31]}}, {instruction[31], instruction[19:12], instruction[30:21], undriven[0]}};  // Bit_Extender bit_extender_4
  Multiplexer #(.select(2), .width(32), .enable("false")) multiplexer_1 (
    .in0(bit_extender_1_out), .in1(bit_extender_2_out), .in2(bit_extender_3_out), .in3(bit_extender_4_out),
    .out(imm_out), .sel(ImmSel));
endmodule

module ControlUnit (
  input  [31:0] instruction,
  output [6:0] out_2,
  output RegWrite,
  output ALUSrc,
  output MemRead,
  output MemWrite,
  output [1:0] MemtoReg,
  output [1:0] ALUOp,
  output Branch,
  output Jump,
  output [1:0] ImmSel
);

  wire comparator_2_eq;

  Comparator #(.width(7)) comparator_1 (.a(instruction[6:0]), .b(7'b0110011), .eq(ALUOp[1]));  // open: gt, lt
  Comparator #(.width(7)) comparator_2 (.a(instruction[6:0]), .b(7'b0010011), .eq(comparator_2_eq));  // open: gt, lt
  Comparator #(.width(7)) comparator_3 (.a(instruction[6:0]), .b(7'b0000011), .eq(MemRead));  // open: gt, lt
  Comparator #(.width(7)) comparator_4 (.a(instruction[6:0]), .b(7'b0100011), .eq(MemWrite));  // open: gt, lt
  Comparator #(.width(7)) comparator_5 (.a(instruction[6:0]), .b(7'b1100011), .eq(ALUOp[0]));  // open: gt, lt
  Comparator #(.width(7)) comparator_6 (.a(instruction[6:0]), .b(7'b1101111), .eq(Jump));  // open: gt, lt
  or or_1 (ImmSel[0], Jump, MemWrite);
  or or_2 (ImmSel[1], Jump, ALUOp[0]);
  or or_3 (RegWrite, ALUOp[1], comparator_2_eq, MemRead, Jump);
  or or_4 (ALUSrc, comparator_2_eq, MemRead, MemWrite);

  assign Branch = ALUOp[0];
  assign MemtoReg = {Jump, MemRead};
  assign out_2 = instruction[6:0];

  // Other names for the same wires on the sheet: opcode[6:0] = instruction[6:0]

  // Notes on the sheet:
  //   alu
  //   alu imm
  //   load
  //   store
  //   branch
  //   jal
  //   R type
  //   I type ALU
  //   I type
  //   S type
  //   B type
  //   J type
endmodule

module PC (
  input  [31:0] d_in,
  input  clk,
  input  clr,
  output [31:0] d_out
);

  Register #(.width(32)) register_1 (.D(d_in), .en(1'b1), .clk(clk), .Q(d_out), .clr(clr));
endmodule

module InstrMem (
  input  [31:0] readAddr,
  output [31:0] instruction
);

  ROM #(.addrWidth(24), .dataWidth(32)) rom_1 (.addr(readAddr[23:0]), .data(instruction));

  // Notes on the sheet:
  //   contents of rom_1 (hex, n*v repeats v):
  //   a00093 300113 2081b3 40208233 60f293 816313 f0c393 412413
endmodule

module ALUControl (
  input  [31:0] instruction,
  input  [1:0] ALU_op,
  output [2:0] ALU_Sel
);

  wire [2:0] rom_1_data;

  ROM #(.addrWidth(6), .dataWidth(3)) rom_1 (.addr({ALU_op, instruction[30], instruction[14:12]}), .data(rom_1_data));
  Multiplexer #(.select(2), .width(3), .enable("false")) multiplexer_1 (
    .in0(3'b000), .in1(3'b001), .in2(rom_1_data), .in3(3'b000), .out(ALU_Sel), .sel(ALU_op));

  // Notes on the sheet:
  //   contents of rom_1 (hex, n*v repeats v):
  //   16*0 16*1 0 0 5 0 4 0 3 2 1 0 5 0 4 0 3 2
endmodule
